// Digital circuit mips_ULA16bits.dig as structural Verilog
module mips_ULA16bits (
  input  in_1,
  input  in_2,
  input  in_3,
  input  in_4,
  input  in_5,
  input  in_6,
  input  in_7,
  input  in_8,
  input  in_9,
  input  in_10,
  input  in_11,
  input  in_12,
  input  in_13,
  input  in_14,
  input  in_15,
  input  in_16,
  input  in_17,
  input  in_18,
  input  in_19,
  input  in_20
);

  mips_ULA8bits_aberta mips_ula8bits_aberta_1 ();  // open: Ainvert, Binvert, CarryIn, Operação, A, B, Less, Saida0, Saida1, Saida2, Saida3, Saida4, Saida5, Saida6, Saida7, CarryOut
  mips_ULA8bits_aberta mips_ula8bits_aberta_2 ();  // open: Ainvert, Binvert, CarryIn, Operação, A, B, Less, Saida0, Saida1, Saida2, Saida3, Saida4, Saida5, Saida6, Saida7, CarryOut
endmodule
