// Digital circuit mips_ULA32bits.dig as structural Verilog
module mips_ULA32bits (
  input  Ainvert,
  input  Binvert,
  input  \Operação ,
  input  CarryIn,
  input  [31:0] A,
  input  [31:0] B,
  output Saida0,
  output Saida1,
  output Saida2,
  output Saida3,
  output Saida4,
  output Saida5,
  output Saida6,
  output Saida7,
  output Saida8,
  output Saida9,
  output Saida10,
  output Saida11,
  output Saida12,
  output Saida13,
  output Saida14,
  output Saida15,
  output Saida16,
  output Saida17,
  output Saida18,
  output Saida19,
  output Saida20,
  output Saida21,
  output Saida22,
  output Saida23,
  output Saida24,
  output Saida25,
  output Saida26,
  output Saida27,
  output Saida28,
  output Saida29,
  output Saida30,
  output Saida31
);

  wire mips_ula16bits_aberta_1_p7, mips_ula16bits_aberta_1_p24;

  // mips_ULA16bits_aberta mips_ula16bits_aberta_1: pin names not known; wires that end beside it: Ainvert, Binvert, \Operação , CarryIn, A[0], B[0], mips_ula16bits_aberta_1_p7, Saida0, Saida1, Saida2, Saida3, Saida4, Saida5, Saida6, Saida7, Saida8, Saida9, Saida10, Saida11, Saida12, Saida13, Saida14, Saida15, mips_ula16bits_aberta_1_p24
  // mips_ULA16bits_aberta mips_ula16bits_aberta_2: pin names not known; wires that end beside it: Ainvert, Binvert, \Operação , mips_ula16bits_aberta_1_p24, A[1], B[1], 1'b0, Saida16, Saida17, Saida18, Saida19, Saida20, Saida21, Saida22, Saida23, Saida24, Saida25, Saida26, Saida27, Saida28, Saida29, Saida30, Saida31, mips_ula16bits_aberta_1_p7
endmodule
