// Digital circuit mips_ULA8bits.dig as structural Verilog
module mips_ULA8bits (
  input  Ainvert,
  input  Binvert,
  input  CarryIn,
  input  [1:0] \Operação ,
  input  [7:0] A,
  input  [7:0] B,
  output Saida0,
  output Saida1,
  output Saida2,
  output Saida3,
  output Saida4,
  output Saida5,
  output Saida6,
  output Saida7
);

  wire mips_ula4bits_aberta_1_carryout, mips_ula4bits_aberta_2_carryout;

  mips_ULA4bits_aberta mips_ula4bits_aberta_1 (
    .Binvert(Binvert), .Ainvert(Ainvert), .CarryIn(CarryIn), .\Operação (\Operação ),
    .Less(mips_ula4bits_aberta_2_carryout), .A(A[3:0]), .B(B[3:0]), .Result0(Saida0), .Result1(Saida1),
    .Result2(Saida2), .Result3(Saida3), .CarryOut(mips_ula4bits_aberta_1_carryout));
  mips_ULA4bits_aberta mips_ula4bits_aberta_2 (
    .Binvert(Binvert), .Ainvert(Ainvert), .CarryIn(mips_ula4bits_aberta_1_carryout), .\Operação (\Operação ),
    .Less(1'b0), .A(A[7:4]), .B(B[7:4]), .Result0(Saida4), .Result1(Saida5), .Result2(Saida6),
    .Result3(Saida7), .CarryOut(mips_ula4bits_aberta_2_carryout));
  // Pins of 1 and 2 bits meet at \Operação 
endmodule
