// Digital circuit mips_bancodeReg.dig as structural Verilog
module mips_bancodeReg (
);

  mips_regleitura mips_regleitura_1 ();  // open: Entrada, Clock, Saida
  mips_mux32 mips_mux32_1 ();  // open: S0, S1, S2, S3, S4, Entrada, Saida
endmodule
